# Fritzing sketch Untitled Sketch 2 (saved by Fritzing 0.9.3b)
breadboards: 1

parts:
  Composant1 = Arduino Uno (Rev3) - ICSP
  LED1 = LED - 5mm [color="Red (633nm)" package="5 mm [THT]"]
  R1 = Photocell (LDR) [package=THT]
  R2 = Resistor [tolerance=±5% resistance=10k package="2010 [SMD]"]
  R3 = Resistor [tolerance=±5% resistance=330 package="2010 [SMD]"]
  S1 = Pushbutton [package="[THT]"]
  U1 = LCD-16X2 [package=lcd-16x2]
  R4 = Resistor [tolerance=±5% resistance=10k package="2010 [SMD]"]
  R5 = Trimmer Potentiometer [maximum_resistance=10kΩ package=THT]
  J1 = Basic Servo

nets:
  N1: Composant1.A0, R1.pin_0, R2.Pin_1
  5V: Composant1.5V, R1.pin_1, U1.VDD, U1.A, R4.Pin_0, R5.leg1, J1.vcc
  N2: Composant1.D9_PWM, J1.pulse
  N3: Composant1.D11_PWM/MOSI, U1.RS
  N4: Composant1.D12/MISO, U1.E
  N5: Composant1.D2, LED1.anode
  N6: Composant1.D3_PWM, S1.Pin_1, S1.Pin_2, R4.Pin_1
  N7: Composant1.D4, U1.DB7
  N8: Composant1.D5_PWM, U1.DB6
  N9: Composant1.D6_PWM, U1.DB5
  N10: Composant1.D7, U1.DB4
  GND: Composant1.GND, R2.Pin_0, R3.Pin_0, S1.Pin_3, S1.Pin_4, U1.VSS, U1.R_W, U1.K, R5.leg2, J1.gnd
  N11: LED1.cathode, R3.Pin_1
  N12: U1.VO, R5.wiper
